# Fritzing sketch Adxl335Test (saved by Fritzing 0.9.0b)
breadboards: 1

parts:
  Parte1 = Triple Axis Accelerometer Breakout - ADXL335
  Parte2 = Arduino Uno (Rev3)

nets:
  N1: Parte1.ZOUT, Parte2.A2
  N2: Parte1.YOUT, Parte2.A1
  N3: Parte1.XOUT, Parte2.A0
  GND: Parte1.GND, Parte2.GND
  VCC: Parte1.VCC, Parte2.AREF, Parte2.3V3

notes:
  Estas son las líneas de datos.s
